# Fritzing sketch Door Pi (saved by Fritzing 0.9.4)
circuit board: 6.80001cm x 5.85cm
breadboards: 1

parts:
  U3 = AQT212GH [package="DIP (Dual Inline) [THT]"]
  U2 = AQT212GH [package="DIP (Dual Inline) [THT]"]
  LED2 = l710a8ge dual led [package=THT]
  LLC1 = Logic Level Converter [package="Breakout board"]
  U1 = TSR2 Series
  R3 = Resistor [tolerance=±5% resistance=470 package=THT]
  PWR = LED - 5mm [color="Red (633nm)" package="5 mm [THT]"]
  R4 = Resistor [tolerance=±5% resistance=470 package=THT]
  R2 = Resistor [tolerance=±5% resistance=470 package=THT]
  R1 = Resistor [tolerance=±5% resistance=470 package=THT]
  U4 = AQT212GH [package="DIP (Dual Inline) [THT]"]
  LED1 = l710a8ge dual led [package=THT]
  12V = 2.1mm DC Barrel Jack Generic
  Power_plug1 = Power plug  # not connected
  Fuse3 = Fuse with Handler [part_number=Htc-15m]
  J1 = Raspberry Pi Header - Pi Hat [package=THT]
  Door_Reader = Camdenboss CTB0158-8 [package=THT]
  R8 = Resistor [tolerance=±5% resistance=330 package=THT]
  R9 = Resistor [tolerance=±5% resistance=330 package=THT]
  Bell_CC = Camdenboss CTB0158-2 [package=THT]
  Strike = Camdenboss CTB0158-2 [package=THT]
  Sensor = Camdenboss CTB0158-2 [package=THT]
  3v3 = Camdenboss CTB0158-2 [package=THT]
  Bell_12V = Camdenboss CTB0158-2 [package=THT]

nets:
  N1: U3.pin1, J1.IO4
  GND: U3.pin2, U2.pin2, LED2.pin2, LED2.pin4, LLC1.L-GND, LLC1.H-GND, U1.GND, PWR.cathode, U4.pin2, LED1.pin2, LED1.pin4, 12V.GND, 12V.sleeve, J1.GND, Door_Reader.pin2, Door_Reader.pin8, Strike.pin1, Sensor.pin1, 3v3.pin1, Bell_12V.pin1
  N2: U3.pin3, U2.pin3, PWR.anode, 12V.center_(V+), Fuse3.Connector2, Door_Reader.pin1
  N3: U3.pin4, R3.Pin_1, Bell_12V.pin2
  N4: U2.pin1, J1.IO17, R8.Pin_0
  N5: U2.pin4, R4.Pin_1, Strike.pin2
  N6: LED2.pin1, R3.Pin_0
  N7: LED2.pin3, R4.Pin_0
  N8: LLC1.LV1, J1.IO14
  N9: LLC1.LV2, J1.IO15
  N10: LLC1.LV, J1.3V3, R8.Pin_1, R9.Pin_1, 3v3.pin2
  N11: LLC1.LV3, J1.IO22#12
  N12: LLC1.LV4, J1.IO22#14
  N13: LLC1.HV4, Door_Reader.pin6
  N14: LLC1.HV3, Door_Reader.pin5
  N15: LLC1.HV, U1.OUT, J1.5V
  N16: LLC1.HV2, Door_Reader.pin4
  N17: LLC1.HV1, Door_Reader.pin3
  N18: U1.IN, Fuse3.Connector1
  N19: R2.Pin_0, LED1.pin3
  N20: R2.Pin_1, J1.IO19
  N21: R1.Pin_0, LED1.pin1
  N22: R1.Pin_1, J1.IO13
  N23: U4.pin1, J1.IO26, R9.Pin_0
  N24: U4.pin3, Bell_CC.pin1
  N25: U4.pin4, Bell_CC.pin2
  N26: J1.IO6, Sensor.pin2

notes:
  5V
  12V
  3.3V
  G-Pi Active
  CuriousJames.net\DIYACPCB
  v1.1
  ¯\_(ツ)_/¯
  R-Spare
  ------>R-Srike On
  ------>G-Bell 12V On

custom parts:
  AQT212GH: PhotoMOS GU 1 Form A High Capacity opto isolator. 4-pin high capacity of 1.1A, I/O isolation voltage of 5,000V
  l710a8ge dual led: KingBright L-710A8GE/11GD-RV T-1 (3mm) BI-LEVEL LED INDICATOR red/green.
  Logic Level Converter: 5V to/from 3.3V logic level converter
  TSR2 Series: Mini DC/DC Step-Down (Buck) Converter - 5V @ 1A output - TSR12450
  2.1mm DC Barrel Jack Generic: 2.1mm DC Barrel Jack with Thru-Hole Connectors (breadboardable)
  Fuse with Handler: Device used to protect against excessive current.
  Raspberry Pi Header - Pi Hat: Raspberry Pi 40 pin header - for creating your own shields. (Mar 2020, bb: make breadboard friendly (.4in pin spacing) and add labels. Schematic add labels. PCB make oblong pins to allow routing traces between the pins.)
  Camdenboss CTB0158-8: Camdenboss CTB0158-8 5.08mm (0.2") Pitch Standard Profile 90 ̊ Rising Clamp Terminal, 8 pole The real-life connectors are modular, made up of two or three connector blocks slotted together. These can be further slotted together to make larger connectors. Fritzing part is derived from Screw terminals by Lionel Michel. Because of the offset between connection pins and screw terminals, these are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
  Camdenboss CTB0158-2: Camdenboss CTB0158-2 5.08mm (0.2") Pitch Standard Profile 90 ̊ Rising Clamp Terminal, 2 pole The real-life connectors are modular, made up of two or three connector blocks slotted together. These can be further slotted together to make larger connectors. Fritzing part is derived from Screw terminals by Lionel Michel. Because of the offset between connection pins and screw terminals, these are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
